# Fritzing sketch Airok (saved by Fritzing 0.9.3b)
breadboards: 1

parts:
  Part1 = Arduino Nano (Rev3.0) (ICSP)
  8-12V = Power plug
  R1 = Resistor [tolerance=±5% resistance=330 package=THT]
  TTP223 = mystery part, 3 pins [chip_label=TTP223]
  BMP180 = Barometric Pressure Sensor - BMP180 Breakout (GY-68)
  R2 = Resistor [tolerance=±5% resistance=10k package=THT]
  R3 = Resistor [tolerance=±5% resistance=10k package=THT]
  Oled_Display = mystery part, 4 pins [chip_label="Oled Disp"]
  DHT11 = DHT11 Humitidy and Temperature Sensor
  R4 = Resistor [tolerance=±5% resistance=10k package=THT]
  U1 = ESP8266 WiFi Module [part_number=ESP8266]
  TGS4161 = mystery part, 5 pins [chip_label=TGS4161]
  LED1 = RGB LED (com. anode, rbg) [package="5 mm [THT]"]
  R5 = Resistor [tolerance=±5% resistance=330 package=THT]
  R6 = Resistor [tolerance=±5% resistance=1k package=THT]
  U2 = Voltage Regulator - 5V [package="TO220 [THT]"]
  C1 = Ceramic Capacitor [capacitance=330nF package="100 mil [THT, multilayer]"]
  C2 = Ceramic Capacitor [capacitance=100nF package="100 mil [THT, multilayer]"]
  U3 = mystery part, 3 pins [chip_label="Regulator 3V3"]
  C3 = Electrolytic Capacitor [capacitance=100µF package="100 mil [THT, electrolytic]"]
  C4 = Electrolytic Capacitor [capacitance=100µF package="100 mil [THT, electrolytic]"]

nets:
  GND: Part1.GND, 8-12V.GND, TTP223.pin1, BMP180.GND, Oled_Display.pin1, DHT11.GND, U1.GND, TGS4161.pin5, LED1.common_anode, U2.GND, C1.0, C2.1, U3.pin1, C3.-, C4.-
  N1: Part1.D2, DHT11.DATA, R4.Pin_0
  N2: Part1.D3, TTP223.pin2
  N3: Part1.D6, U1.RXD
  N4: Part1.D7, U1.TXD
  N5: Part1.D9, R1.Pin_0
  N6: Part1.D10, R5.Pin_0
  VIN: Part1.VIN, 8-12V.VCC, U2.input_voltage, C1.1, U3.pin3, C3.+
  N7: Part1.A5, BMP180.SCL, R2.Pin_0, Oled_Display.pin3
  N8: Part1.A4, BMP180.SDA, R3.Pin_0, Oled_Display.pin4
  N9: Part1.A0, TGS4161.pin3
  N10: Part1.D11/MOSI, R6.Pin_0
  N11: R1.Pin_1, LED1.red_cathode
  N12: TTP223.pin3, DHT11.VDD, R4.Pin_1, TGS4161.pin2, U2.output_voltage, C2.0
  VCC: BMP180.VCC, R2.Pin_1, R3.Pin_1, Oled_Display.pin2, U1.VCC, U1.CH_PD, U3.pin2, C4.+
  N13: LED1.blue_cathode, R5.Pin_1
  N14: LED1.green_cathode, R6.Pin_1

custom parts:
  DHT11 Humitidy and Temperature Sensor: DHT11 Humidity and Temperature Sensor
